# Fritzing sketch circuito_PCB (saved by Fritzing 0.9.3b)
circuit board: 8cm x 9.5cm
perfboards: 1

parts:
  R4 = Resistor [tolerance=±5% resistance=4.7k package=THT]
  R3 = Resistor [tolerance=±5% resistance=4.7k package=THT]
  R2 = Resistor [tolerance=±5% resistance=4.7k package=THT]
  R1 = Resistor [tolerance=±5% resistance=4.7k package=THT]
  U1 = ESP32-38PinWide [part_number=ESP32-38PinWide]
  C1 = Ceramic Capacitor [capacitance=1nF package="200 mil [THT, multilayer]"]
  C2 = Ceramic Capacitor [capacitance=1nF package="200 mil [THT, multilayer]"]
  C3 = Ceramic Capacitor [capacitance=1nF package="200 mil [THT, multilayer]"]
  C4 = Ceramic Capacitor [capacitance=1nF package="200 mil [THT, multilayer]"]

nets:
  N1: R4.Pin_0, R3.Pin_0, R2.Pin_0, R1.Pin_0, U1.3.3
  N2: R4.Pin_1, U1.GPIO25, C1.1
  N3: R3.Pin_1, U1.GPIO33, C2.1
  N4: R2.Pin_1, U1.GPIO32, C3.1
  N5: R1.Pin_1, U1.GPIO35, C4.1
  N6: U1.GND, C1.0, C2.0, C3.0, C4.0

notes:
  r
  g
  b
  5V+
  5V-
  rst_btn
  5V
  GND
  3V3

custom parts:
  ESP32-38PinWide: Generic 38-Pin ESP32 with wide format (only access to one side of pins on a breadboard) based on Stephen Lilley's HiLetgo ESP-WROOM-32 ESP32 ESP-32S Development Board.
